// Logisim project main.circ as structural Verilog: 19 circuits, main circuit main
module main (
);

  wire button_2_out, button_3_out, clk, draw_module_1_drawing, draw_module_1_show, draw_module_1_write, shot;
  wire [2:0] x_vec;
  wire [3:0] hex_to_dec_1_output_1, hex_to_dec_1_output_2, hex_to_dec_2_output_1, hex_to_dec_2_output_2,
       hex_to_dec_3_output_1, hex_to_dec_3_output_2;
  wire [4:0] draw_module_1_line_num, game_1_x, game_1_y;
  wire [15:0] ai_score, game_1_command, game_1_id, hp, player_score;
  wire [31:0] draw_module_1_line, video_buffer_32x32_1_out_5, video_buffer_32x32_1_out_6,
       video_buffer_32x32_1_out_7, video_buffer_32x32_1_out_8, video_buffer_32x32_1_out_9,
       video_buffer_32x32_1_out_10, video_buffer_32x32_1_out_11, video_buffer_32x32_1_out_12,
       video_buffer_32x32_1_out_13, video_buffer_32x32_1_out_14, video_buffer_32x32_1_out_15,
       video_buffer_32x32_1_out_16, video_buffer_32x32_1_out_17, video_buffer_32x32_1_out_18,
       video_buffer_32x32_1_out_19, video_buffer_32x32_1_out_20, video_buffer_32x32_1_out_21,
       video_buffer_32x32_1_out_22, video_buffer_32x32_1_out_23, video_buffer_32x32_1_out_24,
       video_buffer_32x32_1_out_25, video_buffer_32x32_1_out_26, video_buffer_32x32_1_out_27,
       video_buffer_32x32_1_out_28, video_buffer_32x32_1_out_29, video_buffer_32x32_1_out_30,
       video_buffer_32x32_1_out_31, video_buffer_32x32_1_out_32, video_buffer_32x32_1_out_33,
       video_buffer_32x32_1_out_34, video_buffer_32x32_1_out_35, video_buffer_32x32_1_out_36;

  Clock clock_1 (.out(clk));
  draw_module draw_module_1 (
    .clk(clk), .drawing(draw_module_1_drawing), .write(draw_module_1_write), .line(draw_module_1_line),
    .line_num(draw_module_1_line_num), .show(draw_module_1_show), .id(game_1_id), .x(game_1_x), .y(game_1_y),
    .command(game_1_command));
  game game_1 (
    .player_inp_x(x_vec), .ID(game_1_id), .X(game_1_x), .Y(game_1_y), .Command(game_1_command), .clock(clk),
    .drawing(draw_module_1_drawing), .player_score(player_score), .shot(shot), .hp(hp), .ai_score(ai_score));
  DotMatrix #(.inputtype("row"), .matrixcols(32), .matrixrows(32)) dotmatrix_1 (
    .row0(video_buffer_32x32_1_out_5), .row1(video_buffer_32x32_1_out_6), .row2(video_buffer_32x32_1_out_7),
    .row3(video_buffer_32x32_1_out_8), .row4(video_buffer_32x32_1_out_9), .row5(video_buffer_32x32_1_out_10),
    .row6(video_buffer_32x32_1_out_11), .row7(video_buffer_32x32_1_out_12),
    .row8(video_buffer_32x32_1_out_13), .row9(video_buffer_32x32_1_out_14),
    .row10(video_buffer_32x32_1_out_15), .row11(video_buffer_32x32_1_out_16),
    .row12(video_buffer_32x32_1_out_17), .row13(video_buffer_32x32_1_out_18),
    .row14(video_buffer_32x32_1_out_19), .row15(video_buffer_32x32_1_out_20),
    .row16(video_buffer_32x32_1_out_21), .row17(video_buffer_32x32_1_out_22),
    .row18(video_buffer_32x32_1_out_23), .row19(video_buffer_32x32_1_out_24),
    .row20(video_buffer_32x32_1_out_25), .row21(video_buffer_32x32_1_out_26),
    .row22(video_buffer_32x32_1_out_27), .row23(video_buffer_32x32_1_out_28),
    .row24(video_buffer_32x32_1_out_29), .row25(video_buffer_32x32_1_out_30),
    .row26(video_buffer_32x32_1_out_31), .row27(video_buffer_32x32_1_out_32),
    .row28(video_buffer_32x32_1_out_33), .row29(video_buffer_32x32_1_out_34),
    .row30(video_buffer_32x32_1_out_35), .row31(video_buffer_32x32_1_out_36));
  video_buffer_32x32 video_buffer_32x32_1 (
    .out_5(video_buffer_32x32_1_out_5), .out_6(video_buffer_32x32_1_out_6),
    .out_7(video_buffer_32x32_1_out_7), .out_8(video_buffer_32x32_1_out_8),
    .out_9(video_buffer_32x32_1_out_9), .out_10(video_buffer_32x32_1_out_10),
    .out_11(video_buffer_32x32_1_out_11), .out_12(video_buffer_32x32_1_out_12),
    .out_13(video_buffer_32x32_1_out_13), .out_14(video_buffer_32x32_1_out_14),
    .out_15(video_buffer_32x32_1_out_15), .out_16(video_buffer_32x32_1_out_16),
    .out_17(video_buffer_32x32_1_out_17), .out_18(video_buffer_32x32_1_out_18),
    .out_19(video_buffer_32x32_1_out_19), .out_20(video_buffer_32x32_1_out_20),
    .out_21(video_buffer_32x32_1_out_21), .out_22(video_buffer_32x32_1_out_22),
    .out_23(video_buffer_32x32_1_out_23), .out_24(video_buffer_32x32_1_out_24),
    .out_25(video_buffer_32x32_1_out_25), .out_26(video_buffer_32x32_1_out_26),
    .out_27(video_buffer_32x32_1_out_27), .out_28(video_buffer_32x32_1_out_28),
    .out_29(video_buffer_32x32_1_out_29), .out_30(video_buffer_32x32_1_out_30),
    .out_31(video_buffer_32x32_1_out_31), .out_32(video_buffer_32x32_1_out_32),
    .out_33(video_buffer_32x32_1_out_33), .out_34(video_buffer_32x32_1_out_34),
    .out_35(video_buffer_32x32_1_out_35), .out_36(video_buffer_32x32_1_out_36), .write(draw_module_1_write),
    .\input (draw_module_1_line), .y(draw_module_1_line_num), .show(draw_module_1_show));
  Button button_1 (.out(shot));
  Button button_2 (.out(button_2_out));
  Button button_3 (.out(button_3_out));
  movement_controller movement_controller_1 (.left(button_2_out), .right(button_3_out), .x_vec(x_vec));
  Hex_Digit_Display hex_digit_display_1 (.value(hex_to_dec_1_output_2));  // open: dp
  Hex_Digit_Display hex_digit_display_2 (.value(hex_to_dec_1_output_1));  // open: dp
  hex_to_dec hex_to_dec_1 (.input_hex(hp), .output_2(hex_to_dec_1_output_2), .output_1(hex_to_dec_1_output_1));
  Hex_Digit_Display hex_digit_display_3 (.value(hex_to_dec_2_output_1));  // open: dp
  Hex_Digit_Display hex_digit_display_4 (.value(hex_to_dec_2_output_2));  // open: dp
  hex_to_dec hex_to_dec_2 (
    .input_hex(player_score), .output_2(hex_to_dec_2_output_2), .output_1(hex_to_dec_2_output_1));
  Hex_Digit_Display hex_digit_display_5 (.value(hex_to_dec_3_output_2));  // open: dp
  Hex_Digit_Display hex_digit_display_6 (.value(hex_to_dec_3_output_1));  // open: dp
  hex_to_dec hex_to_dec_3 (.input_hex(ai_score), .output_2(hex_to_dec_3_output_2), .output_1(hex_to_dec_3_output_1));

  // Notes on the sheet:
  //   Shoot
  //   Movement
  //   <-
  //   ->
  //   HP
  //   PLAYER SCORE
  //   BOT SCORE
endmodule

module CDM16 (
  input  [15:0] adr,
  input  [15:0] val,
  input  clock,
  input  write,
  input  hold,
  input  end_cycle,
  output drawing,
  output [15:0] id,
  output [15:0] x,
  output [15:0] y,
  output [15:0] command,
  output \wait ,
  output run,
  output button,
  output lose,
  output win,
  output [15:0] hp,
  output [15:0] player_score,
  output [15:0] ai_score
);

  wire and_2_out, and_3_out, and_4_out, and_5_out, and_6_out, and_7_out, and_8_out, and_9_out, and_10_out,
       and_11_out, and_12_out, and_13_out, and_14_out, and_15_out, and_16_out, bit_extender_1_out,
       cdm_16_1_p3, cdm_16_1_p4, \checker , code, comparator_1_eq, comparator_2_eq, comparator_7_eq,
       comparator_8_eq, comparator_9_eq, comparator_10_eq, comparator_11_eq, comparator_12_eq,
       comparator_14_eq, d_ff_1_q, data, decoder_1_out0, decoder_1_out1, initialized, mem, not_1_out,
       not_2_out, not_3_out, not_4_out, not_5_out, not_7_out, or_1_out, or_2_out, pull_resistor_4_node,
       pull_resistor_7_node, pull_resistor_8_node, pull_resistor_9_node, pull_resistor_10_node,
       pull_resistor_17_node, read_write, transistor_3_out, word, write_t;
  wire [15:0] cdm_16_1_p8, cdm_16_1_p9, cdm_16_1_p10, controlled_buffer_2_out, register_1_q, register_2_q,
       register_3_q, register_4_q, register_5_q, register_6_q, register_7_q, register_8_q, register_9_q,
       transistor_4_out;

  and and_1 (write_t, write, d_ff_1_q);
  D_Flip_Flop d_ff_1 (.clk(not_1_out), .D(or_1_out), .Q(d_ff_1_q));  // open: Qn, preset, en, reset
  not not_1 (not_1_out, clock);
  or or_1 (or_1_out, write, and_2_out, or_2_out);
  buf or_2 (or_2_out, hold);  // OR_Gate
  and and_2 (and_2_out, ~initialized, \checker );  // AND_Gate
  // CdM_16 cdm_16_1: pin names not known; wires that end beside it: d_ff_1_q, clock, cdm_16_1_p3, cdm_16_1_p4, mem, read_write, word, cdm_16_1_p8, cdm_16_1_p9, cdm_16_1_p10
  // Probe on cdm_16_1_p3
  not not_2 (not_2_out, write_t);
  not not_3 (not_3_out, write_t);
  assign cdm_16_1_p10 = and_4_out ? controlled_buffer_2_out : 16'bz;  // Controlled_Buffer controlled_buffer_1
  assign controlled_buffer_2_out = and_3_out ? cdm_16_1_p9 : 16'bz;  // Controlled_Buffer controlled_buffer_2
  and and_3 (and_3_out, not_2_out, not_4_out);
  not not_4 (not_4_out, read_write);
  not not_5 (not_5_out, read_write);
  and and_4 (and_4_out, not_3_out, read_write);
  Transistor transistor_1 (.in(decoder_1_out0), .out(code), .gate(write_t));
  Pull_Resistor pull_resistor_1 (.node(code));
  Pull_Resistor #(.pull(1)) pull_resistor_2 (.node(data));
  Transistor #(.gate("br")) transistor_2 (.in(decoder_1_out1), .out(data), .gate(write_t));
  Decoder #(.disabled(0)) decoder_1 (.out0(decoder_1_out0), .out1(decoder_1_out1), .sel(cdm_16_1_p4), .en(mem));
  Transistor transistor_3 (.in(not_5_out), .out(transistor_3_out), .gate(write_t));
  Pull_Resistor #(.pull(1)) pull_resistor_3 (.node(transistor_3_out));
  Transistor #(.\type ("n"), .width(16)) transistor_4 (.in(adr), .out(transistor_4_out), .gate(write_t));
  Transistor #(.gate("br"), .width(16)) transistor_5 (.in(cdm_16_1_p8), .out(transistor_4_out), .gate(write_t));
  // Probe on transistor_4_out
  Pull_Resistor #(.pull(1)) pull_resistor_4 (.node(pull_resistor_4_node));
  Transistor transistor_6 (.in(word), .out(pull_resistor_4_node), .gate(write_t));
  Comparator #(.width(16)) comparator_1 (.a(transistor_4_out), .b(16'h86), .eq(comparator_1_eq));  // open: gt, lt
  Pull_Resistor pull_resistor_5 (.node(comparator_1_eq));
  Comparator #(.width(16)) comparator_2 (.a(transistor_4_out), .b(16'h88), .eq(comparator_2_eq));  // open: gt, lt
  Pull_Resistor pull_resistor_6 (.node(comparator_2_eq));
  Pull_Resistor pull_resistor_7 (.node(pull_resistor_7_node));
  Comparator #(.width(16)) comparator_3 (.a(transistor_4_out), .b(16'h8a), .eq(pull_resistor_7_node));  // open: gt, lt
  Pull_Resistor pull_resistor_8 (.node(pull_resistor_8_node));
  Comparator #(.width(16)) comparator_4 (.a(transistor_4_out), .b(16'h8c), .eq(pull_resistor_8_node));  // open: gt, lt
  Pull_Resistor pull_resistor_9 (.node(pull_resistor_9_node));
  Comparator #(.width(16)) comparator_5 (.a(transistor_4_out), .b(16'h84), .eq(pull_resistor_9_node));  // open: gt, lt
  Pull_Resistor pull_resistor_10 (.node(pull_resistor_10_node));
  Comparator #(.width(16)) comparator_6 (.a(transistor_4_out), .b(16'h96), .eq(pull_resistor_10_node));  // open: gt, lt
  Comparator #(.width(16)) comparator_7 (.a(transistor_4_out), .b(16'ha0), .eq(comparator_7_eq));  // open: gt, lt
  Pull_Resistor pull_resistor_11 (.node(comparator_7_eq));
  Comparator #(.width(16)) comparator_8 (.a(transistor_4_out), .b(16'h9c), .eq(comparator_8_eq));  // open: gt, lt
  Pull_Resistor pull_resistor_12 (.node(comparator_8_eq));
  Comparator #(.width(16)) comparator_9 (.a(transistor_4_out), .b(16'hae), .eq(comparator_9_eq));  // open: gt, lt
  Pull_Resistor pull_resistor_13 (.node(comparator_9_eq));
  Comparator #(.width(16)) comparator_10 (.a(transistor_4_out), .b(16'hb0), .eq(comparator_10_eq));  // open: gt, lt
  Pull_Resistor pull_resistor_14 (.node(comparator_10_eq));
  Comparator #(.width(16)) comparator_11 (.a(transistor_4_out), .b(16'hc6), .eq(comparator_11_eq));  // open: gt, lt
  Pull_Resistor pull_resistor_15 (.node(comparator_11_eq));
  Comparator #(.width(16)) comparator_12 (.a(transistor_4_out), .b(16'hc8), .eq(comparator_12_eq));  // open: gt, lt
  Pull_Resistor pull_resistor_16 (.node(comparator_12_eq));
  Pull_Resistor pull_resistor_17 (.node(pull_resistor_17_node));
  Transistor #(.gate("br")) transistor_7 (.in(read_write), .out(pull_resistor_17_node), .gate(write_t));
  // ROM rom_1: pin names not known; wires that end beside it: transistor_4_out, code, word, controlled_buffer_2_out
  // RAM ram_1: pin names not known; wires that end beside it: transistor_4_out, pull_resistor_4_node, data, clock, pull_resistor_17_node, controlled_buffer_2_out
  Register #(.width(16)) register_1 (.D(controlled_buffer_2_out), .Q(register_1_q), .clk(and_5_out));  // open: en, clr
  and and_5 (and_5_out, comparator_1_eq, data, transistor_3_out);
  Register #(.width(16)) register_2 (.D(controlled_buffer_2_out), .Q(register_2_q), .clk(and_6_out));  // open: en, clr
  and and_6 (and_6_out, comparator_2_eq, data, transistor_3_out);
  Register #(.width(16)) register_3 (.D(controlled_buffer_2_out), .Q(register_3_q), .clk(and_7_out));  // open: en, clr
  and and_7 (and_7_out, pull_resistor_7_node, data, transistor_3_out);
  Register #(.width(16)) register_4 (.D(controlled_buffer_2_out), .Q(register_4_q), .clk(and_8_out));  // open: en, clr
  and and_8 (and_8_out, pull_resistor_8_node, data, transistor_3_out);
  Register #(.width(16)) register_5 (
    .D(controlled_buffer_2_out), .Q(register_5_q), .clk(and_9_out), .clr(end_cycle));  // open: en
  and and_9 (and_9_out, pull_resistor_9_node, data, transistor_3_out);
  Register #(.width(16)) register_6 (.D(controlled_buffer_2_out), .Q(register_6_q), .clk(and_10_out));  // open: en, clr
  and and_10 (and_10_out, pull_resistor_10_node, data, transistor_3_out);
  Register #(.width(16)) register_7 (.D(controlled_buffer_2_out), .Q(register_7_q), .clk(and_11_out));  // open: en, clr
  and and_11 (and_11_out, comparator_7_eq, data, transistor_3_out);
  Register #(.width(16)) register_8 (.D(controlled_buffer_2_out), .Q(register_8_q), .clk(and_12_out));  // open: en, clr
  and and_12 (and_12_out, comparator_8_eq, data, transistor_3_out);
  Register #(.width(16)) register_9 (.D(controlled_buffer_2_out), .Q(register_9_q), .clk(and_13_out));  // open: en, clr
  and and_13 (and_13_out, comparator_9_eq, data, transistor_3_out);
  Register #(.width(16)) register_10 (.D(controlled_buffer_2_out), .Q(hp), .clk(and_14_out));  // open: en, clr
  and and_14 (and_14_out, comparator_10_eq, data, transistor_3_out);
  Register #(.width(16)) register_11 (
    .D(controlled_buffer_2_out), .Q(player_score), .clk(and_15_out));  // open: en, clr
  and and_15 (and_15_out, comparator_11_eq, data, transistor_3_out);
  Register #(.width(16)) register_12 (.D(controlled_buffer_2_out), .Q(ai_score), .clk(and_16_out));  // open: en, clr
  and and_16 (and_16_out, comparator_12_eq, data, transistor_3_out);
  Transistor #(.\type ("n"), .width(16)) transistor_8 (.in(val), .out(controlled_buffer_2_out), .gate(write_t));
  assign id = drawing ? register_1_q : 16'bz;  // Controlled_Buffer controlled_buffer_3
  assign x = drawing ? register_2_q : 16'bz;  // Controlled_Buffer controlled_buffer_4
  assign y = drawing ? register_3_q : 16'bz;  // Controlled_Buffer controlled_buffer_5
  assign command = drawing ? register_4_q : 16'bz;  // Controlled_Buffer controlled_buffer_6
  Bit_Extender #(.in_width(16), .out_width(1)) bit_extender_1 (.in(register_6_q), .out(bit_extender_1_out));
  Bit_Extender #(.in_width(16), .out_width(1)) bit_extender_2 (.in(register_7_q), .out(button));
  Bit_Extender #(.in_width(16), .out_width(1)) bit_extender_3 (.in(register_8_q), .out(lose));
  Bit_Extender #(.in_width(16), .out_width(1)) bit_extender_4 (.in(register_9_q), .out(win));
  Comparator #(.width(16), .mode("unsigned")) comparator_13 (
    .a(register_5_q), .b(16'h2), .eq(drawing));  // open: gt, lt
  Comparator #(.width(16), .mode("unsigned")) comparator_14 (
    .a(register_5_q), .b({16{1'b0}}), .eq(comparator_14_eq));  // open: gt, lt
  not not_6 (\wait , comparator_14_eq);
  not not_7 (not_7_out, drawing);
  xor xor_1 (run, not_7_out, bit_extender_1_out);
  Register #(.width(1)) u_initialized (.D(run), .Q(initialized), .clk(run));  // open: en, clr

  // Other names for the same wires on the sheet: cl = clock; draw = drawing; end = end_cycle

  // Notes on the sheet:
  //   hold приостанавливает процессор
  //   write как hold но даёт возможность писать в ОЗУ
  //   run
endmodule

module game (
  input  [2:0] player_inp_x,
  input  shot,
  input  clock,
  input  drawing,
  output [4:0] X,
  output [4:0] Y,
  output [15:0] ID,
  output [15:0] Command,
  output [15:0] hp,
  output [15:0] player_score,
  output [15:0] ai_score
);

  wire and_1_out, and_2_out, and_3_out, and_4_out, and_7_out, and_8_out, button, cdm16_1_drawing,
       collide_check_enemy, collide_check_player, collide_check_wall, command_draw, command_show,
       comparator_5_eq, comparator_7_eq, comparator_8_eq, end_cycle, enemies_multiobject_1_ready,
       enemy_initing, hold, int_enemy, int_player, lose, not_1_out, or_4_out, or_5_out, player_initing,
       processor_draw, processor_drawing, pull_resistor_7_node, register_1_q, register_3_q, run,
       update_pl_pos, \wait , wait_int, win, write;
  wire [4:0] enemies_multiobject_1_debug__enemy_cout;
  wire [5:0] enemies_multiobject_1_proc_command;
  wire [15:0] bit_extender_1_out, check2_writer_1_adr, check2_writer_1_val, collided, divider_1_out,
       divider_2_out, divider_3_out, divider_4_out, enemies_multiobject_1_x, enemies_multiobject_1_y,
       player_x_q, player_y_q, register_2_q, subtractor_1_out, x_col, y_col;

  assign bit_extender_1_out = {{13{1'b0}}, player_inp_x};  // Bit_Extender bit_extender_1
  or or_1 (hold, enemy_initing, player_initing, processor_drawing);
  or or_2 (\wait , wait_int, write, drawing);
  or or_3 (end_cycle, win, lose);
  Pull_Resistor pull_resistor_1 (.node(collided));
  Subtractor #(.width(16)) subtractor_1 (.a(bit_extender_1_out), .b(16'h4), .out(subtractor_1_out));  // open: bin, bout
  // Probe on enemies_multiobject_1_debug__enemy_cout
  enemies_multiobject enemies_multiobject_1 (
    .\wait (\wait ), .draw(run), .id(ID), .y(enemies_multiobject_1_y), .x(enemies_multiobject_1_x),
    .command(Command), .ready(enemies_multiobject_1_ready), .initing(enemy_initing),
    .collide_check(collide_check_enemy), .clock(clock),
    .DEBUG__enemy_cout(enemies_multiobject_1_debug__enemy_cout),
    .proc_command(enemies_multiobject_1_proc_command), .end_cycle(end_cycle), .x_col(x_col), .y_col(y_col),
    .collided(collided));
  Pull_Resistor pull_resistor_2 (.node(command_draw));
  Comparator #(.width(16), .mode("unsigned")) comparator_1 (.a(Command), .b(16'h1), .eq(command_draw));  // open: gt, lt
  Pull_Resistor pull_resistor_3 (.node(command_show));
  Comparator #(.width(16), .mode("unsigned")) comparator_2 (.a(Command), .b(16'h2), .eq(command_show));  // open: gt, lt
  Pull_Resistor pull_resistor_4 (.node(int_player));
  Comparator #(.width(6), .mode("unsigned")) comparator_3 (
    .a(enemies_multiobject_1_proc_command), .b({6{1'b0}}), .eq(int_player));  // open: gt, lt
  Pull_Resistor pull_resistor_5 (.node(int_enemy));
  Comparator #(.width(6), .mode("unsigned")) comparator_4 (
    .a(enemies_multiobject_1_proc_command), .b(6'b000001), .eq(int_enemy));  // open: gt, lt
  player_object player_object_1 (
    .draw(enemies_multiobject_1_ready), .ready(processor_draw), .id(ID), .x_2(enemies_multiobject_1_x),
    .y(enemies_multiobject_1_y), .x(subtractor_1_out), .command(Command), .\wait (\wait ), .clock(clock),
    .proc_command(enemies_multiobject_1_proc_command), .initing(player_initing), .end_cycle(end_cycle),
    .x_col(x_col), .y_col(y_col), .collide_check(collide_check_player), .collided(collided));
  // Probe on ID
  // Probe on enemies_multiobject_1_x
  // Probe on enemies_multiobject_1_y
  // Probe on Command
  Register #(.width(1)) register_1 (
    .D(processor_draw), .Q(register_1_q), .clk(processor_draw), .clr(and_1_out));  // open: en
  and and_1 (and_1_out, ~drawing, register_1_q);  // AND_Gate
  Divider #(.width(16)) divider_1 (.a(enemies_multiobject_1_x), .b(16'h2), .out(divider_1_out));  // open: upper, rem
  Bit_Extender #(.in_width(16), .out_width(5)) bit_extender_2 (.in(divider_1_out), .out(X));
  // Probe on X
  win_multiobject win_multiobject_1 (
    .\wait (\wait ), .draw(win), .id(ID), .x(enemies_multiobject_1_x), .y(enemies_multiobject_1_y),
    .command(Command), .clock(clock));  // open: ready
  check2_writer check2_writer_1 (
    .adr(check2_writer_1_adr), .val(check2_writer_1_val), .write(write), .run(and_1_out), .clock(clock));
  // Probe on Y
  Bit_Extender #(.in_width(16), .out_width(5)) bit_extender_3 (.in(divider_2_out), .out(Y));
  Divider #(.width(16)) divider_2 (.a(enemies_multiobject_1_y), .b(16'h2), .out(divider_2_out));  // open: upper, rem
  not not_1 (not_1_out, comparator_5_eq);
  Comparator #(.width(16), .mode("unsigned")) comparator_5 (
    .a(collided), .b({16{1'b0}}), .eq(comparator_5_eq));  // open: gt, lt
  lose_multiobject lose_multiobject_1 (
    .\wait (\wait ), .draw(lose), .id(ID), .x(enemies_multiobject_1_x), .y(enemies_multiobject_1_y),
    .command(Command), .clock(clock));  // open: ready
  Register #(.width(16)) register_2 (.D(collided), .Q(register_2_q), .clk(not_1_out));  // open: en, clr
  collision_writer collision_writer_1 (
    .adr(check2_writer_1_adr), .val(check2_writer_1_val), .write(write), .run(not_1_out), .clock(clock),
    .collided(register_2_q));
  enemy_writer enemy_writer_1 (
    .x(enemies_multiobject_1_x), .y(enemies_multiobject_1_y), .adr(check2_writer_1_adr),
    .val(check2_writer_1_val), .write(write), .clock(clock), .run(and_2_out));
  and and_2 (and_2_out, command_draw, int_enemy);
  and and_3 (and_3_out, shot, ~button);  // AND_Gate
  Register #(.width(1)) register_3 (.D(and_3_out), .Q(register_3_q), .clk(and_3_out), .clr(and_4_out));  // open: en
  and and_4 (and_4_out, register_3_q, ~write);  // AND_Gate
  and and_5 (update_pl_pos, int_player, command_draw);
  Register #(.width(16)) player_x (.D(enemies_multiobject_1_x), .Q(player_x_q), .clk(update_pl_pos));  // open: en, clr
  Register #(.width(16)) player_y (.D(enemies_multiobject_1_y), .Q(player_y_q), .clk(update_pl_pos));  // open: en, clr
  shot_writer shot_writer_1 (
    .adr(check2_writer_1_adr), .val(check2_writer_1_val), .run(and_4_out), .write(write), .clock(clock),
    .x(player_x_q), .y(player_y_q));
  Pull_Resistor pull_resistor_6 (.node(write));
  CDM16 cdm16_1 (
    .adr(check2_writer_1_adr), .val(check2_writer_1_val), .id(ID), .x(enemies_multiobject_1_x),
    .y(enemies_multiobject_1_y), .command(Command), .write(write), .hold(hold), .clock(clock),
    .\wait (wait_int), .run(run), .drawing(cdm16_1_drawing), .button(button), .lose(lose), .win(win),
    .hp(hp), .end_cycle(end_cycle), .player_score(player_score), .ai_score(ai_score));
  Divider #(.width(16)) divider_3 (.a(enemies_multiobject_1_x), .b(16'h2), .out(divider_3_out));  // open: upper, rem
  Register #(.width(16)) x_3 (.D(divider_3_out), .Q(x_col), .clk(or_5_out));  // open: en, clr
  Pull_Resistor pull_resistor_7 (.node(pull_resistor_7_node));
  Comparator #(.width(16), .mode("unsigned")) comparator_6 (
    .a(ID), .b(16'hf), .eq(pull_resistor_7_node));  // open: gt, lt
  Comparator #(.width(16), .mode("unsigned")) comparator_7 (.a(ID), .b(16'ha), .eq(comparator_7_eq));  // open: gt, lt
  Comparator #(.width(16), .mode("unsigned")) comparator_8 (.a(ID), .b(16'h14), .eq(comparator_8_eq));  // open: gt, lt
  Divider #(.width(16)) divider_4 (.a(enemies_multiobject_1_y), .b(16'h2), .out(divider_4_out));  // open: upper, rem
  Register #(.width(16)) y_3 (.D(divider_4_out), .Q(y_col), .clk(or_5_out));  // open: en, clr
  and and_6 (processor_drawing, cdm16_1_drawing, drawing);
  Pull_Resistor pull_resistor_8 (.node(comparator_7_eq));
  or or_4 (or_4_out, comparator_7_eq, comparator_8_eq);
  Pull_Resistor pull_resistor_9 (.node(comparator_8_eq));
  and and_7 (and_7_out, command_draw, pull_resistor_7_node);
  and and_8 (and_8_out, command_draw, or_4_out);
  or or_5 (or_5_out, and_8_out, and_7_out);
  D_Flip_Flop d_ff_1 (.clk(clock), .D(and_7_out), .Q(collide_check_player));  // open: Qn, preset, en, reset
  D_Flip_Flop d_ff_2 (.clk(clock), .D(and_8_out), .Q(collide_check_enemy));  // open: Qn, preset, en, reset
  D_Flip_Flop d_ff_3 (.clk(clock), .D(or_5_out), .Q(collide_check_wall));  // open: Qn, preset, en, reset

  // Other names for the same wires on the sheet: clk = clock
endmodule

module draw_module (
  input  clk,
  input  [15:0] command,
  input  [15:0] id,
  input  [4:0] x,
  input  [4:0] y,
  output drawing,
  output write,
  output [31:0] line,
  output show,
  output [4:0] line_num
);

  wire activator_q, and_1_out, comparator_1_eq, counter_1_carry, drawing_t, not_1_out, transistor_1_out;
  wire [4:0] counter_1_q;
  wire [15:0] adder_1_out, bit_extender_1_out, multiplier_1_out;
  wire [31:0] rom_1_data;

  simple_drawer_32x32 simple_drawer_32x32_1 (
    .x(x), .y(y), .texture_line(counter_1_q), .texture_input(rom_1_data), .cur_line(line_num), .line_x1(line));
  Counter #(.width(5), .max('h2)) counter_1 (
    .Q(counter_1_q), .carry(counter_1_carry), .clk(transistor_1_out), .clr(and_1_out));  // open: load, D, count
  Transistor #(.\type ("n"), .gate("br")) transistor_1 (.in(clk), .out(transistor_1_out), .gate(drawing_t));
  and and_1 (and_1_out, ~clk, counter_1_carry);  // AND_Gate
  D_Flip_Flop #(.trigger("falling")) synchronizer (
    .clk(clk), .D(activator_q), .Q(drawing_t), .reset(and_1_out));  // open: Qn, preset, en
  D_Flip_Flop activator (
    .clk(comparator_1_eq), .D(comparator_1_eq), .Q(activator_q), .reset(and_1_out));  // open: Qn, preset, en
  or or_1 (drawing, drawing_t, activator_q, and_1_out);
  assign bit_extender_1_out = {{11{1'b0}}, counter_1_q};  // Bit_Extender bit_extender_1
  Multiplier #(.width(16)) multiplier_1 (.a(id), .b(16'h3), .out(multiplier_1_out));  // open: cin, cout
  // Probe on id
  Adder #(.width(16)) adder_1 (.a(bit_extender_1_out), .b(multiplier_1_out), .out(adder_1_out));  // open: cin, cout
  Comparator #(.width(16), .mode("unsigned")) comparator_1 (
    .a(command), .b(16'h1), .eq(comparator_1_eq));  // open: gt, lt
  Pull_Resistor pull_resistor_1 (.node(comparator_1_eq));
  Comparator #(.width(16), .mode("unsigned")) comparator_2 (.a(command), .b(16'h2), .eq(show));  // open: gt, lt
  Pull_Resistor pull_resistor_2 (.node(show));
  and and_2 (write, drawing_t, not_1_out);
  not not_1 (not_1_out, clk);
  ROM #(.addrWidth(16), .dataWidth(32)) rom_1 (.addr(adder_1_out), .data(rom_1_data));  // open: sel

  // Other names for the same wires on the sheet: cmd_show = show

  // Notes on the sheet:
  //   texture line counter
  //   contents of rom_1 (hex, n*v repeats v):
  //   2 7 5 2 5 5 0 0 0 2 7 5 2 5 5 7 5 5 2 7 7 2 5 7 2 5 5 0 0 0 1 1 1 1151 1351 1551 1955 1155 114a
  //   7ce381 41441 3ce441 50441 51441 7ce39f 1 2 1 0 0 0 2 1 0 2 3 0 3 3 0 1 1 1
endmodule

module video_buffer_32x32 (
  input  write,
  input  [31:0] \input ,
  input  [4:0] y,
  input  show,
  output [31:0] out_5,
  output [31:0] out_6,
  output [31:0] out_7,
  output [31:0] out_8,
  output [31:0] out_9,
  output [31:0] out_10,
  output [31:0] out_11,
  output [31:0] out_12,
  output [31:0] out_13,
  output [31:0] out_14,
  output [31:0] out_15,
  output [31:0] out_16,
  output [31:0] out_17,
  output [31:0] out_18,
  output [31:0] out_19,
  output [31:0] out_20,
  output [31:0] out_21,
  output [31:0] out_22,
  output [31:0] out_23,
  output [31:0] out_24,
  output [31:0] out_25,
  output [31:0] out_26,
  output [31:0] out_27,
  output [31:0] out_28,
  output [31:0] out_29,
  output [31:0] out_30,
  output [31:0] out_31,
  output [31:0] out_32,
  output [31:0] out_33,
  output [31:0] out_34,
  output [31:0] out_35,
  output [31:0] out_36
);

  wire _0, _1, _2, _3, _4, _5, _6, _7, _8, _9, _10, _11, _12, _13, _14, _15, _16, _17, _18, _19, _20, _21,
       _22, _23, _24, _25, _26, _27, _28, _29, _30, _31;
  wire [31:0] r0, r1, r2, r3, r4, r5, r6, r7, r8, r9, r10, r11, r12, r13, r14, r15, r16, r17, r18, r19, r20,
       r21, r22, r23, r24, r25, r26, r27, r28, r29, r30, r31;

  Demultiplexer #(.select(5), .disabled(0)) demultiplexer_1 (
    .out0(_0), .out1(_1), .out2(_2), .out3(_3), .out4(_4), .out5(_5), .out6(_6), .out7(_7), .out8(_8),
    .out9(_9), .out10(_10), .out11(_11), .out12(_12), .out13(_13), .out14(_14), .out15(_15), .out16(_16),
    .out17(_17), .out18(_18), .out19(_19), .out20(_20), .out21(_21), .out22(_22), .out23(_23), .out24(_24),
    .out25(_25), .out26(_26), .out27(_27), .out28(_28), .out29(_29), .out30(_30), .out31(_31), .in(1'b1),
    .sel(y), .en(write));
  _32buffer_el u_32buffer_el_1 (
    .\input (\input ), ._1___buffer_read(_0), .out_5(r0), .video(out_5), ._1___buffer_write___clr(show));
  _32buffer_el u_32buffer_el_2 (
    .\input (\input ), ._1___buffer_read(_1), .out_5(r1), .video(out_6), ._1___buffer_write___clr(show));
  _32buffer_el u_32buffer_el_3 (
    .\input (\input ), ._1___buffer_read(_2), .out_5(r2), .video(out_7), ._1___buffer_write___clr(show));
  _32buffer_el u_32buffer_el_4 (
    .\input (\input ), ._1___buffer_read(_3), .out_5(r3), .video(out_8), ._1___buffer_write___clr(show));
  _32buffer_el u_32buffer_el_5 (
    .\input (\input ), ._1___buffer_read(_4), .out_5(r4), .video(out_9), ._1___buffer_write___clr(show));
  _32buffer_el u_32buffer_el_6 (
    .\input (\input ), ._1___buffer_read(_5), .out_5(r5), .video(out_10), ._1___buffer_write___clr(show));
  _32buffer_el u_32buffer_el_7 (
    .\input (\input ), ._1___buffer_read(_6), .out_5(r6), .video(out_11), ._1___buffer_write___clr(show));
  _32buffer_el u_32buffer_el_8 (
    .\input (\input ), ._1___buffer_read(_7), .out_5(r7), .video(out_12), ._1___buffer_write___clr(show));
  _32buffer_el u_32buffer_el_9 (
    .\input (\input ), ._1___buffer_read(_8), .out_5(r8), .video(out_13), ._1___buffer_write___clr(show));
  _32buffer_el u_32buffer_el_10 (
    .\input (\input ), ._1___buffer_read(_9), .out_5(r9), .video(out_14), ._1___buffer_write___clr(show));
  _32buffer_el u_32buffer_el_11 (
    .\input (\input ), ._1___buffer_read(_10), .out_5(r10), .video(out_15), ._1___buffer_write___clr(show));
  _32buffer_el u_32buffer_el_12 (
    .\input (\input ), ._1___buffer_read(_11), .out_5(r11), .video(out_16), ._1___buffer_write___clr(show));
  _32buffer_el u_32buffer_el_13 (
    .\input (\input ), ._1___buffer_read(_12), .out_5(r12), .video(out_17), ._1___buffer_write___clr(show));
  _32buffer_el u_32buffer_el_14 (
    .\input (\input ), ._1___buffer_read(_13), .out_5(r13), .video(out_18), ._1___buffer_write___clr(show));
  _32buffer_el u_32buffer_el_15 (
    .\input (\input ), ._1___buffer_read(_14), .out_5(r14), .video(out_19), ._1___buffer_write___clr(show));
  _32buffer_el u_32buffer_el_16 (
    .\input (\input ), ._1___buffer_read(_15), .out_5(r15), .video(out_20), ._1___buffer_write___clr(show));
  _32buffer_el u_32buffer_el_17 (
    .\input (\input ), ._1___buffer_read(_16), .out_5(r16), .video(out_21), ._1___buffer_write___clr(show));
  _32buffer_el u_32buffer_el_18 (
    .\input (\input ), ._1___buffer_read(_17), .out_5(r17), .video(out_22), ._1___buffer_write___clr(show));
  _32buffer_el u_32buffer_el_19 (
    .\input (\input ), ._1___buffer_read(_18), .out_5(r18), .video(out_23), ._1___buffer_write___clr(show));
  _32buffer_el u_32buffer_el_20 (
    .\input (\input ), ._1___buffer_read(_19), .out_5(r19), .video(out_24), ._1___buffer_write___clr(show));
  _32buffer_el u_32buffer_el_21 (
    .\input (\input ), ._1___buffer_read(_20), .out_5(r20), .video(out_25), ._1___buffer_write___clr(show));
  _32buffer_el u_32buffer_el_22 (
    .\input (\input ), ._1___buffer_read(_21), .out_5(r21), .video(out_26), ._1___buffer_write___clr(show));
  _32buffer_el u_32buffer_el_23 (
    .\input (\input ), ._1___buffer_read(_22), .out_5(r22), .video(out_27), ._1___buffer_write___clr(show));
  _32buffer_el u_32buffer_el_24 (
    .\input (\input ), ._1___buffer_read(_23), .out_5(r23), .video(out_28), ._1___buffer_write___clr(show));
  _32buffer_el u_32buffer_el_25 (
    .\input (\input ), ._1___buffer_read(_24), .out_5(r24), .video(out_29), ._1___buffer_write___clr(show));
  _32buffer_el u_32buffer_el_26 (
    .\input (\input ), ._1___buffer_read(_25), .out_5(r25), .video(out_30), ._1___buffer_write___clr(show));
  _32buffer_el u_32buffer_el_27 (
    .\input (\input ), ._1___buffer_read(_26), .out_5(r26), .video(out_31), ._1___buffer_write___clr(show));
  _32buffer_el u_32buffer_el_28 (
    .\input (\input ), ._1___buffer_read(_27), .out_5(r27), .video(out_32), ._1___buffer_write___clr(show));
  _32buffer_el u_32buffer_el_29 (
    .\input (\input ), ._1___buffer_read(_28), .out_5(r28), .video(out_33), ._1___buffer_write___clr(show));
  _32buffer_el u_32buffer_el_30 (
    .\input (\input ), ._1___buffer_read(_29), .out_5(r29), .video(out_34), ._1___buffer_write___clr(show));
  _32buffer_el u_32buffer_el_31 (
    .\input (\input ), ._1___buffer_read(_30), .out_5(r30), .video(out_35), ._1___buffer_write___clr(show));
  _32buffer_el u_32buffer_el_32 (
    .\input (\input ), ._1___buffer_read(_31), .out_5(r31), .video(out_36), ._1___buffer_write___clr(show));

  // Other names for the same wires on the sheet: inp[31:0] = \input ; w = show

  // Notes on the sheet:
  //   write: pull=down
endmodule

module _32buffer_el (
  input  [31:0] \input ,
  input  _1___buffer_read,
  input  _1___buffer_write___clr,
  output [31:0] video,
  output [31:0] out_5
);

  wire [31:0] or_1_out;

  assign or_1_out = \input  | out_5;  // OR_Gate or_1, 32 bits wide
  Register #(.width(32)) buffer (
    .D(or_1_out), .Q(out_5), .clk(_1___buffer_read), .clr(_1___buffer_write___clr));  // open: en
  Register #(.width(32)) u_video (.D(out_5), .Q(video), .clk(_1___buffer_write___clr));  // open: en, clr
endmodule

module simple_drawer_32x32 (
  input  [4:0] texture_line,
  input  [31:0] texture_input,
  input  [4:0] x,
  input  [4:0] y,
  output [4:0] cur_line,
  output [31:0] line_x1
);

  wire [31:0] n32_bit_reverse_1_out_2;

  // Probe on x
  // Probe on y
  Adder #(.width(5)) adder_1 (.a(texture_line), .b(y), .out(cur_line));  // open: cin, cout
  _32_bit_reverse u_32_bit_reverse_1 (.in_1(texture_input), .out_2(n32_bit_reverse_1_out_2));
  Pull_Resistor pull_resistor_1 (.node(x));
  Shifter #(.width(32), .shift("lr")) shifter_1 (.in(n32_bit_reverse_1_out_2), .\dist (x), .out(line_x1));
endmodule

module _32_bit_reverse (
  input  [31:0] in_1,
  output [31:0] out_2
);


  assign out_2 = {in_1[0], in_1[1], in_1[2], in_1[3], in_1[4], in_1[5], in_1[6], in_1[7], in_1[8], in_1[9], in_1[10], in_1[11], in_1[12], in_1[13], in_1[14], in_1[15], in_1[16], in_1[17], in_1[18], in_1[19], in_1[20], in_1[21], in_1[22], in_1[23], in_1[24], in_1[25], in_1[26], in_1[27], in_1[28], in_1[29], in_1[30], in_1[31]};
endmodule

module player_object (
  input  collide_check,
  input  [15:0] x,
  input  \wait ,
  input  [15:0] x_col,
  input  end_cycle,
  input  draw,
  input  clock,
  input  [15:0] y_col,
  output [15:0] collided,
  output initing,
  output [15:0] id,
  output [15:0] x_2,
  output [15:0] y,
  output [15:0] command,
  output [5:0] proc_command,
  output ready
);

  wire and_1_out, and_2_out, and_3_out, collided_t, comparator_1_eq, comparator_2_lt, comparator_3_eq,
       comparator_3_gt, comparator_4_gt, counter_1_carry, d_ff_1_q, draw_t, init_step, not_1_out, not_3_out,
       not_4_out, not_5_out, not_6_out, not_7_out, not_8_out, or_1_out, or_2_out, register_1_q, register_2_q,
       transistor_1_out;
  wire [1:0] counter_1_q;
  wire [2:0] counter_2_q;
  wire [5:0] controlled_buffer_5_out;
  wire [15:0] adder_1_out, controlled_buffer_1_out, controlled_buffer_2_out, controlled_buffer_3_out,
       controlled_buffer_4_out, divider_1_out, divider_2_out, multiplexer_2_out, multiplexer_3_out,
       subtractor_1_out, subtractor_2_out, x_t;

  Bit_Extender #(.in_width(2), .out_width(1)) bit_extender_1 (.in(counter_1_q), .out(init_step));
  Counter #(.width(2), .max('h2)) counter_1 (
    .Q(counter_1_q), .carry(counter_1_carry), .clk(clock), .clr(register_1_q));  // open: load, D, count
  or or_1 (or_1_out, end_cycle, ready);
  Register #(.width(1)) register_1 (.D(counter_1_carry), .Q(register_1_q), .clk(counter_1_carry));  // open: en, clr
  not not_1 (not_1_out, \wait );
  Register #(.width(1)) register_2 (.D(draw), .Q(register_2_q), .clk(draw), .clr(or_1_out));  // open: en
  not not_2 (initing, register_1_q);
  Counter #(.width(3), .max('h2)) counter_2 (
    .Q(counter_2_q), .carry(ready), .clk(transistor_1_out), .clr(ready));  // open: load, D, count
  Transistor #(.\type ("n")) transistor_1 (.in(clock), .out(transistor_1_out), .gate(and_1_out));
  and and_1 (and_1_out, not_1_out, register_2_q);
  Multiplexer #(.enable("false")) multiplexer_1 (.in0(register_2_q), .in1(init_step), .out(draw_t), .sel(initing));
  not not_3 (not_3_out, collided_t);
  Adder #(.width(16)) adder_1 (.a(x_t), .b(multiplexer_2_out), .out(adder_1_out));  // open: cin, cout
  Multiplexer #(.width(16), .enable("false")) multiplexer_2 (
    .in0(x), .in1(16'ha), .out(multiplexer_2_out), .sel(initing));
  Comparator #(.width(3), .mode("unsigned")) comparator_1 (
    .a(counter_2_q), .b(3'b001), .eq(comparator_1_eq));  // open: gt, lt
  Transistor #(.\type ("n"), .width(16)) transistor_2 (.in(16'h1), .out(collided), .gate(d_ff_1_q));
  D_Flip_Flop #(.trigger("falling")) d_ff_1 (
    .clk(clock), .D(collided_t), .Q(d_ff_1_q), .reset(not_3_out));  // open: Qn, preset, en
  Register #(.width(16)) u_x (.D(adder_1_out), .Q(x_t), .clk(draw_t));  // open: en, clr
  Multiplexer #(.width(16), .enable("false")) multiplexer_3 (
    .in0({16{1'b0}}), .in1(16'h1), .out(multiplexer_3_out), .sel(comparator_1_eq));
  assign controlled_buffer_1_out = draw_t ? {16{1'b0}} : 16'bz;  // Controlled_Buffer controlled_buffer_1
  not not_4 (not_4_out, initing);
  assign controlled_buffer_2_out = draw_t ? x_t : 16'bz;  // Controlled_Buffer controlled_buffer_2
  not not_5 (not_5_out, initing);
  assign controlled_buffer_3_out = draw_t ? 16'h38 : 16'bz;  // Controlled_Buffer controlled_buffer_3
  not not_6 (not_6_out, initing);
  assign controlled_buffer_4_out = draw_t ? multiplexer_3_out : 16'bz;  // Controlled_Buffer controlled_buffer_4
  not not_7 (not_7_out, initing);
  assign controlled_buffer_5_out = draw_t ? {6{1'b0}} : 6'bz;  // Controlled_Buffer controlled_buffer_5
  not not_8 (not_8_out, initing);
  assign id = not_4_out ? controlled_buffer_1_out : 16'bz;  // Controlled_Buffer controlled_buffer_6
  assign x_2 = not_5_out ? controlled_buffer_2_out : 16'bz;  // Controlled_Buffer controlled_buffer_7
  assign y = not_6_out ? controlled_buffer_3_out : 16'bz;  // Controlled_Buffer controlled_buffer_8
  assign command = not_7_out ? controlled_buffer_4_out : 16'bz;  // Controlled_Buffer controlled_buffer_9
  assign proc_command = not_8_out ? controlled_buffer_5_out : 6'bz;  // Controlled_Buffer controlled_buffer_10
  Pull_Resistor pull_resistor_1 (.node(x_col));
  Pull_Resistor pull_resistor_2 (.node(y_col));
  // Probe on x_col
  Divider #(.width(16)) divider_1 (.a(x_t), .b(16'h2), .out(divider_1_out));  // open: upper, rem
  // Probe on y_col
  Divider #(.width(16)) divider_2 (.a(16'h38), .b(16'h2), .out(divider_2_out));  // open: upper, rem
  Subtractor #(.width(16)) subtractor_1 (.a(x_col), .b(divider_1_out), .out(subtractor_1_out));  // open: bin, bout
  // Probe on subtractor_2_out
  Subtractor #(.width(16)) subtractor_2 (.a(y_col), .b(divider_2_out), .out(subtractor_2_out));  // open: bin, bout
  // Probe on 16'hfffd
  Comparator #(.width(16)) comparator_2 (.a(subtractor_1_out), .b(16'h3), .lt(comparator_2_lt));  // open: gt, eq
  Comparator #(.width(16)) comparator_3 (
    .a(subtractor_1_out), .b({16{1'b0}}), .gt(comparator_3_gt), .eq(comparator_3_eq));  // open: lt
  Comparator #(.width(16)) comparator_4 (.a(subtractor_2_out), .b(16'hfffd), .gt(comparator_4_gt));  // open: eq, lt
  and and_2 (and_2_out, comparator_2_lt, or_2_out);
  or or_2 (or_2_out, comparator_3_gt, comparator_3_eq);
  and and_3 (and_3_out, and_2_out, comparator_4_gt);
  and and_4 (collided_t, and_3_out, collide_check);

  // Other names for the same wires on the sheet: clk = clock
endmodule

module enemies_multiobject (
  input  collide_check,
  input  \wait ,
  input  end_cycle,
  input  draw,
  input  [15:0] x_col,
  input  clock,
  input  [15:0] y_col,
  output [15:0] collided,
  output [15:0] id,
  output initing,
  output [15:0] y,
  output [4:0] DEBUG__enemy_cout,
  output [15:0] x,
  output [15:0] command,
  output [5:0] proc_command,
  output ready
);

  wire alive, and_1_out, and_2_out, and_3_out, and_4_out, and_6_out, and_7_out, and_8_out, and_9_out,
       and_10_out, and_11_out, and_12_out, collided_t, comparator_1_eq, comparator_1_gt, comparator_2_eq,
       comparator_2_lt, comparator_4_lt, comparator_5_eq, comparator_5_lt, comparator_6_eq, comparator_6_lt,
       comparator_8_eq, comparator_8_lt, counter_1_carry, draw_t, may_collide, multiplexer_2_out, not_1_out,
       not_2_out, not_3_out, not_5_out, not_6_out, not_7_out, or_1_out, or_2_out, or_4_out, or_5_out,
       or_6_out, or_7_out, or_8_out, or_9_out, or_10_out, or_11_out, or_12_out, pull_resistor_1_node,
       pull_resistor_2_node, pull_resistor_3_node, register_1_q, register_2_q, register_4_q, register_5_q,
       register_8_q, register_9_q, texture_state, wait_t, x_aligned, xnor_1_out;
  wire [4:0] col_adr, counter_1_q;
  wire [15:0] adder_1_out, adder_2_out, adder_3_out, adder_4_out, adder_5_out, adder_6_out, adder_7_out,
       adder_8_out, bit_extender_1_out, controlled_buffer_4_out, divider_1_out, divider_1_rem, divider_2_out,
       divider_3_out, divider_4_out, divider_4_rem, divider_5_out, divider_5_rem, multiplexer_3_out,
       multiplexer_4_out, multiplexer_5_out, multiplexer_6_out, multiplier_1_out, multiplier_2_out,
       multiplier_3_out, multiplier_4_out, multiplier_5_out, negator_1_out, negator_2_out, register_10_q,
       register_11_q, subtractor_1_out, subtractor_2_out, subtractor_3_out, x_t, y_t;

  not not_1 (not_1_out, may_collide);
  and and_1 (and_1_out, collided_t, alive);
  D_Flip_Flop #(.trigger("falling")) d_ff_1 (
    .clk(clock), .D(may_collide), .Q(collided_t), .reset(not_1_out));  // open: Qn, preset, en
  Register #(.width(1)) register_1 (.D(or_1_out), .Q(register_1_q), .clk(clock));  // open: en, clr
  or or_1 (or_1_out, collide_check, \wait );
  Register #(.width(1)) register_2 (.D(draw), .Q(register_2_q), .clk(draw), .clr(or_2_out));  // open: en
  or or_2 (or_2_out, end_cycle, ready);
  Transistor #(.\type ("n"), .width(16)) transistor_1 (.in(16'h2), .out(collided), .gate(and_1_out));
  or or_3 (wait_t, register_1_q, or_1_out);
  Register #(.width(1)) register_3 (.D(register_2_q), .Q(draw_t), .clk(and_2_out), .clr(or_2_out));  // open: en
  and and_2 (and_2_out, clock, ~wait_t);  // AND_Gate
  Counter #(.width(5), .max('he)) counter_1 (
    .Q(counter_1_q), .carry(counter_1_carry), .clk(not_3_out));  // open: load, D, count, clr
  Multiplexer #(.width(5), .enable("false")) multiplexer_1 (
    .in0(counter_1_q), .in1(col_adr), .out(DEBUG__enemy_cout), .sel(may_collide));
  not not_2 (not_2_out, counter_1_carry);
  not not_3 (not_3_out, multiplexer_2_out);
  Multiplexer #(.enable("false")) multiplexer_2 (
    .in0(clock), .in1(pull_resistor_1_node), .out(multiplexer_2_out), .sel(register_4_q));
  Pull_Resistor pull_resistor_1 (.node(pull_resistor_1_node));
  Transistor #(.\type ("n"), .gate("br")) transistor_2 (.in(or_4_out), .out(pull_resistor_1_node), .gate(draw_t));
  or or_4 (or_4_out, wait_t, and_3_out);
  and and_3 (and_3_out, ~clock, ~and_4_out);  // AND_Gate
  not not_4 (initing, register_4_q);
  Register #(.width(1)) register_4 (.D(not_2_out), .Q(register_4_q), .clk(not_2_out));  // open: en, clr
  Negator #(.width(16)) negator_1 (.in(16'h1), .out(negator_1_out));
  assign bit_extender_1_out = {{11{1'b0}}, DEBUG__enemy_cout};  // Bit_Extender bit_extender_1
  Pull_Resistor pull_resistor_2 (.node(pull_resistor_2_node));
  Transistor #(.gate("br")) transistor_3 (.in(1'b1), .out(pull_resistor_2_node), .gate(register_4_q));
  xnor xnor_1 (xnor_1_out, collided_t, register_4_q);
  Register #(.width(1)) register_5 (.D(not_2_out), .Q(register_5_q), .clk(not_2_out), .clr(register_5_q));  // open: en
  Multiplexer #(.width(16), .enable("false")) multiplexer_3 (
    .in0(16'h1), .in1(negator_1_out), .out(multiplexer_3_out), .sel(register_8_q));
  RAM #(.addrWidth(5), .dataWidth(1), .bus("separate")) ram_1 (
    .addr(DEBUG__enemy_cout), .din(pull_resistor_2_node), .data(alive), .str(xnor_1_out), .clk(clock));  // open: sel, ld, clr
  // Probe on subtractor_1_out
  Adder #(.width(16)) adder_1 (.a(x_t), .b(multiplexer_3_out), .out(adder_1_out));  // open: cin, cout
  Adder #(.width(16)) adder_2 (.a(16'h2), .b(y_t), .out(adder_2_out));  // open: cin, cout
  and and_4 (and_4_out, alive, register_4_q);
  and and_5 (ready, register_5_q, draw_t);
  Register #(.width(16)) register_6 (.D(adder_1_out), .Q(x_t), .clk(draw_t));  // open: en, clr
  Register #(.width(16)) register_7 (.D(adder_2_out), .Q(y_t), .clk(and_6_out));  // open: en, clr
  and and_6 (and_6_out, register_9_q, ready);
  Divider #(.width(16)) divider_1 (
    .a(bit_extender_1_out), .b(16'h5), .out(divider_1_out), .rem(divider_1_rem));  // open: upper
  Counter #(.width(1), .max('h1)) counter_2 (
    .Q(texture_state), .clk(register_5_q));  // open: load, D, count, carry, clr
  // Probe on negator_2_out
  or or_5 (or_5_out, comparator_1_gt, comparator_1_eq);
  Comparator #(.width(16), .mode("unsigned")) comparator_1 (
    .a(x_t), .b(subtractor_1_out), .gt(comparator_1_gt), .eq(comparator_1_eq));  // open: lt
  Multiplier #(.width(16)) multiplier_1 (.a(divider_1_out), .b(16'ha), .out(multiplier_1_out));  // open: cin, cout
  Multiplier #(.width(16)) multiplier_2 (.a(divider_1_rem), .b(16'ha), .out(multiplier_2_out));  // open: cin, cout
  Multiplexer #(.width(16), .enable("false")) multiplexer_4 (
    .in0({16{1'b0}}), .in1(16'h1), .out(multiplexer_4_out), .sel(and_7_out));
  and and_7 (and_7_out, and_4_out, or_6_out);
  or or_6 (or_6_out, not_5_out, wait_t);
  not not_5 (not_5_out, clock);
  Comparator #(.width(16)) comparator_2 (
    .a(x_t), .b(negator_2_out), .eq(comparator_2_eq), .lt(comparator_2_lt));  // open: gt
  Adder #(.width(16)) adder_3 (.a(16'h3), .b(divider_1_out), .out(adder_3_out));  // open: cin, cout
  Adder #(.width(16)) adder_4 (.a(16'h6), .b(divider_1_out), .out(adder_4_out));  // open: cin, cout
  Adder #(.width(16)) adder_5 (.a(y_t), .b(multiplier_1_out), .out(adder_5_out));  // open: cin, cout
  Adder #(.width(16)) adder_6 (.a(x_t), .b(multiplier_2_out), .out(adder_6_out));  // open: cin, cout
  or or_7 (or_7_out, comparator_2_eq, comparator_2_lt);
  Register #(.width(1)) register_8 (.D(or_5_out), .Q(register_8_q), .clk(or_5_out), .clr(and_8_out));  // open: en
  Register #(.width(1)) register_9 (.D(or_8_out), .Q(register_9_q), .clk(or_8_out), .clr(and_6_out));  // open: en
  or or_8 (or_8_out, or_5_out, and_8_out);
  Multiplexer #(.width(16), .enable("false")) multiplexer_5 (
    .in0(adder_3_out), .in1(adder_4_out), .out(multiplexer_5_out), .sel(texture_state));
  assign id = draw_t ? multiplexer_5_out : 16'bz;  // Controlled_Buffer controlled_buffer_1
  assign y = draw_t ? adder_5_out : 16'bz;  // Controlled_Buffer controlled_buffer_2
  assign x = draw_t ? adder_6_out : 16'bz;  // Controlled_Buffer controlled_buffer_3
  assign controlled_buffer_4_out = alive ? divider_1_rem : 16'bz;  // Controlled_Buffer controlled_buffer_4
  assign command = draw_t ? multiplexer_4_out : 16'bz;  // Controlled_Buffer controlled_buffer_5
  assign proc_command = draw_t ? 6'b000001 : 6'bz;  // Controlled_Buffer controlled_buffer_6
  and and_8 (and_8_out, or_7_out, register_8_q);
  and and_9 (and_9_out, pull_resistor_3_node, wait_t);
  Pull_Resistor pull_resistor_3 (.node(pull_resistor_3_node));
  Comparator #(.width(16), .mode("unsigned")) comparator_3 (
    .a(controlled_buffer_4_out), .b(register_11_q), .gt(pull_resistor_3_node));  // open: eq, lt
  Multiplexer #(.width(16), .enable("false")) multiplexer_6 (
    .in0(16'h30), .in1(controlled_buffer_4_out), .out(multiplexer_6_out), .sel(draw_t));
  Register #(.width(16)) register_10 (.D(multiplexer_6_out), .Q(register_10_q), .clk(or_9_out));  // open: en, clr
  or or_9 (or_9_out, and_10_out, and_11_out);
  and and_10 (and_10_out, comparator_4_lt, wait_t);
  Comparator #(.width(16), .mode("unsigned")) comparator_4 (
    .a(controlled_buffer_4_out), .b(register_10_q), .lt(comparator_4_lt));  // open: gt, eq
  Pull_Resistor pull_resistor_4 (.node(comparator_4_lt));
  Register #(.width(16)) register_11 (
    .D(controlled_buffer_4_out), .Q(register_11_q), .clk(and_9_out), .clr(not_6_out));  // open: en
  not not_6 (not_6_out, draw_t);
  Pull_Resistor pull_resistor_5 (.node(x_col));
  Pull_Resistor pull_resistor_6 (.node(y_col));
  Multiplier #(.width(16)) multiplier_3 (.a(16'h8), .b(adder_7_out), .out(multiplier_3_out));  // open: cin, cout
  Adder #(.width(16)) adder_7 (.a(16'h1), .b(register_11_q), .out(adder_7_out));  // open: cin, cout
  // Probe on x_col
  Divider #(.width(16)) divider_2 (.a(x_t), .b(16'h2), .out(divider_2_out));  // open: upper, rem
  // Probe on divider_2_out
  Divider #(.width(16)) divider_3 (.a(y_t), .b(16'h2), .out(divider_3_out));  // open: upper, rem
  not not_7 (not_7_out, draw_t);
  and and_11 (and_11_out, not_7_out, clock);
  Negator #(.width(16)) negator_2 (.in(multiplier_4_out), .out(negator_2_out));
  Multiplier #(.width(16)) multiplier_4 (.a(register_10_q), .b(16'ha), .out(multiplier_4_out));  // open: cin, cout
  Subtractor #(.width(16)) subtractor_1 (.a(16'h3b), .b(multiplier_3_out), .out(subtractor_1_out));  // open: bin, bout
  // Probe on subtractor_2_out
  Subtractor #(.width(16)) subtractor_2 (.a(x_col), .b(divider_2_out), .out(subtractor_2_out));  // open: bin, bout
  // Probe on divider_4_rem
  Subtractor #(.width(16)) subtractor_3 (.a(y_col), .b(divider_3_out), .out(subtractor_3_out));  // open: bin, bout
  Divider #(.width(16)) divider_4 (
    .a(subtractor_2_out), .b(16'h5), .out(divider_4_out), .rem(divider_4_rem));  // open: upper
  Comparator #(.width(16), .mode("unsigned")) comparator_5 (
    .a(divider_4_rem), .b(16'h2), .eq(comparator_5_eq), .lt(comparator_5_lt));  // open: gt
  Divider #(.width(16)) divider_5 (
    .a(subtractor_3_out), .b(16'h5), .out(divider_5_out), .rem(divider_5_rem));  // open: upper
  Comparator #(.width(16), .mode("unsigned")) comparator_6 (
    .a(divider_5_rem), .b(16'h2), .eq(comparator_6_eq), .lt(comparator_6_lt));  // open: gt
  Comparator #(.width(16), .mode("unsigned")) comparator_7 (
    .a(divider_4_out), .b(16'h6), .lt(x_aligned));  // open: gt, eq
  // Probe on divider_4_out
  or or_10 (or_10_out, comparator_5_eq, comparator_5_lt);
  and and_12 (and_12_out, or_10_out, or_11_out);
  Multiplier #(.width(16)) multiplier_5 (.a(divider_5_out), .b(16'h5), .out(multiplier_5_out));  // open: cin, cout
  // Probe on multiplier_5_out
  or or_11 (or_11_out, comparator_6_eq, comparator_6_lt);
  // Probe on adder_8_out
  Adder #(.width(16)) adder_8 (.a(divider_4_out), .b(multiplier_5_out), .out(adder_8_out));  // open: cin, cout
  Comparator #(.width(16), .mode("unsigned")) comparator_8 (
    .a(adder_8_out), .b(16'he), .eq(comparator_8_eq), .lt(comparator_8_lt));  // open: gt
  Bit_Extender #(.in_width(16), .out_width(5)) bit_extender_2 (.in(adder_8_out), .out(col_adr));
  or or_12 (or_12_out, comparator_8_eq, comparator_8_lt);
  and and_13 (may_collide, or_12_out, and_12_out, collide_check, x_aligned);

  // Other names for the same wires on the sheet: clk = clock

  // Notes on the sheet:
  //   enemy matrix
  //   enemies in row
  //   rows delta
  //   columns delta
  //   base texture id1
  //   base texture id2
  //   output X
  //   output Y
endmodule

module win_multiobject (
  input  \wait ,
  input  draw,
  input  clock,
  output [15:0] id,
  output [15:0] x,
  output [15:0] y,
  output [15:0] command,
  output ready
);

  wire and_1_out, comparator_1_eq, draw_t, not_1_out, not_2_out, register_1_q, transistor_1_out;
  wire [3:0] counter_1_q;
  wire [15:0] bit_extender_1_out, multiplexer_1_out, multiplexer_2_out, multiplexer_3_out, multiplexer_4_out;

  Register #(.width(1)) register_1 (.D(draw), .Q(register_1_q), .clk(draw), .clr(ready));  // open: en
  Register #(.width(1)) register_2 (.D(register_1_q), .Q(draw_t), .clk(not_1_out), .clr(ready));  // open: en
  not not_1 (not_1_out, clock);
  not not_2 (not_2_out, \wait );
  Counter #(.width(4), .max('h5)) counter_1 (
    .Q(counter_1_q), .carry(ready), .clk(transistor_1_out), .clr(ready));  // open: load, D, count
  Transistor #(.\type ("n")) transistor_1 (.in(clock), .out(transistor_1_out), .gate(and_1_out));
  and and_1 (and_1_out, not_2_out, draw_t);
  Multiplexer #(.width(16), .enable("false")) multiplexer_1 (
    .in0(16'hb), .in1(16'hc), .out(multiplexer_1_out), .sel(counter_1_q[1]));
  Multiplexer #(.width(16), .enable("false")) multiplexer_2 (
    .in0(16'h1a), .in1(16'h20), .out(multiplexer_2_out), .sel(counter_1_q[1]));
  Comparator #(.width(4), .mode("unsigned")) comparator_1 (
    .a(counter_1_q), .b(4'b0000), .eq(comparator_1_eq));  // open: gt, lt
  assign bit_extender_1_out = {{15{1'b0}}, counter_1_q[0]};  // Bit_Extender bit_extender_1
  assign id = draw_t ? multiplexer_1_out : 16'bz;  // Controlled_Buffer controlled_buffer_1
  assign x = draw_t ? 16'h10 : 16'bz;  // Controlled_Buffer controlled_buffer_2
  assign y = draw_t ? multiplexer_2_out : 16'bz;  // Controlled_Buffer controlled_buffer_3
  Multiplexer #(.width(16), .enable("false")) multiplexer_3 (
    .in0(multiplexer_4_out), .in1(16'h2), .out(multiplexer_3_out), .sel(comparator_1_eq));
  Multiplexer #(.width(16), .enable("false")) multiplexer_4 (
    .in0(bit_extender_1_out), .in1(16'h2), .out(multiplexer_4_out), .sel(counter_1_q[2]));
  assign command = draw_t ? multiplexer_3_out : 16'bz;  // Controlled_Buffer controlled_buffer_4

  // Other names for the same wires on the sheet: clk = clock
endmodule

module lose_multiobject (
  input  \wait ,
  input  draw,
  input  clock,
  output [15:0] id,
  output [15:0] x,
  output [15:0] y,
  output [15:0] command,
  output ready
);

  wire and_1_out, comparator_1_eq, draw_t, not_1_out, not_2_out, register_1_q, transistor_1_out;
  wire [3:0] counter_1_q;
  wire [15:0] bit_extender_1_out, multiplexer_1_out, multiplexer_2_out, multiplexer_3_out, multiplexer_4_out;

  Register #(.width(1)) register_1 (.D(draw), .Q(register_1_q), .clk(draw), .clr(ready));  // open: en
  Register #(.width(1)) register_2 (.D(register_1_q), .Q(draw_t), .clk(not_1_out), .clr(ready));  // open: en
  not not_1 (not_1_out, clock);
  not not_2 (not_2_out, \wait );
  Counter #(.width(4), .max('hf)) counter_1 (
    .Q(counter_1_q), .carry(ready), .clk(transistor_1_out), .clr(ready));  // open: load, D, count
  Transistor #(.\type ("n")) transistor_1 (.in(clock), .out(transistor_1_out), .gate(and_1_out));
  and and_1 (and_1_out, not_2_out, draw_t);
  Multiplexer #(.width(16), .enable("false")) multiplexer_1 (
    .in0(16'hd), .in1(16'he), .out(multiplexer_1_out), .sel(counter_1_q[1]));
  Multiplexer #(.width(16), .enable("false")) multiplexer_2 (
    .in0(16'h1a), .in1(16'h20), .out(multiplexer_2_out), .sel(counter_1_q[1]));
  Comparator #(.width(4), .mode("unsigned")) comparator_1 (
    .a(counter_1_q), .b(4'b0000), .eq(comparator_1_eq));  // open: gt, lt
  assign bit_extender_1_out = {{15{1'b0}}, counter_1_q[0]};  // Bit_Extender bit_extender_1
  assign id = draw_t ? multiplexer_1_out : 16'bz;  // Controlled_Buffer controlled_buffer_1
  assign x = draw_t ? 16'h8 : 16'bz;  // Controlled_Buffer controlled_buffer_2
  assign y = draw_t ? multiplexer_2_out : 16'bz;  // Controlled_Buffer controlled_buffer_3
  Multiplexer #(.width(16), .enable("false")) multiplexer_3 (
    .in0(multiplexer_4_out), .in1(16'h2), .out(multiplexer_3_out), .sel(comparator_1_eq));
  Multiplexer #(.width(16), .enable("false")) multiplexer_4 (
    .in0(bit_extender_1_out), .in1(16'h2), .out(multiplexer_4_out), .sel(counter_1_q[2]));
  assign command = draw_t ? multiplexer_3_out : 16'bz;  // Controlled_Buffer controlled_buffer_4

  // Other names for the same wires on the sheet: clk = clock
endmodule

module enemy_writer (
  input  [15:0] y,
  input  [15:0] x,
  input  run,
  input  clock,
  output [15:0] val,
  output [15:0] adr,
  output write
);

  wire activate_q, counter_1_carry, not_1_out, not_2_out, pull_resistor_1_node, writing;
  wire [2:0] counter_1_q, random_1_out;
  wire [15:0] bit_extender_1_out, multiplexer_1_out, multiplexer_2_out;

  Pull_Resistor pull_resistor_1 (.node(pull_resistor_1_node));
  assign pull_resistor_1_node = writing ? clock : 1'bz;  // Controlled_Buffer controlled_buffer_1
  Random #(.width(3)) random_1 (.clk(pull_resistor_1_node), .out(random_1_out));  // open: next, clr
  assign bit_extender_1_out = {{13{1'b0}}, random_1_out};  // Bit_Extender bit_extender_1
  Counter #(.width(3), .max('h5)) counter_1 (
    .Q(counter_1_q), .carry(counter_1_carry), .clk(not_1_out), .clr(not_2_out));  // open: load, D, count
  not not_1 (not_1_out, clock);
  Multiplexer #(.select(3), .width(16), .enable("false")) multiplexer_1 (
    .in0({16{1'b0}}), .in1(16'h80), .in2(16'h82), .in3(16'hac), .in4(16'h84), .out(multiplexer_1_out),
    .sel(counter_1_q));  // open: in5, in6, in7
  Multiplexer #(.select(3), .width(16), .enable("false")) multiplexer_2 (
    .in0({16{1'b0}}), .in1(x), .in2(y), .in3(bit_extender_1_out), .in4(16'h1), .out(multiplexer_2_out),
    .sel(counter_1_q));  // open: in5, in6, in7
  D_Flip_Flop activate (.clk(run), .D(run), .Q(activate_q), .reset(counter_1_carry));  // open: Qn, preset, en
  assign adr = writing ? multiplexer_1_out : 16'bz;  // Controlled_Buffer controlled_buffer_2
  // Probe on multiplexer_1_out
  assign val = writing ? multiplexer_2_out : 16'bz;  // Controlled_Buffer controlled_buffer_3
  // Probe on multiplexer_2_out
  not not_2 (not_2_out, writing);
  buf buffer_1 (write, writing);
  D_Flip_Flop #(.trigger("falling")) synchronizer (
    .clk(clock), .D(activate_q), .Q(writing), .reset(counter_1_carry));  // open: Qn, preset, en

  // Other names for the same wires on the sheet: clk = clock

  // Notes on the sheet:
  //   buffer_1 drives only 1 and floats otherwise
endmodule

module check2_writer (
  input  run,
  input  clock,
  output [15:0] adr,
  output [15:0] val,
  output write
);

  wire activator_q, counter_1_carry, not_1_out, writing;
  wire [1:0] counter_1_q;
  wire [15:0] multiplexer_1_out, multiplexer_2_out;

  Counter #(.width(2), .max('h2)) counter_1 (
    .Q(counter_1_q), .carry(counter_1_carry), .clk(clock), .clr(not_1_out));  // open: load, D, count
  Multiplexer #(.select(2), .width(16), .enable("false")) multiplexer_1 (
    .in0({16{1'b0}}), .in1(16'h84), .out(multiplexer_1_out), .sel(counter_1_q));  // open: in2, in3
  Multiplexer #(.select(2), .width(16), .enable("false")) multiplexer_2 (
    .in0({16{1'b0}}), .in1(16'h2), .out(multiplexer_2_out), .sel(counter_1_q));  // open: in2, in3
  D_Flip_Flop activator (.clk(run), .D(run), .Q(activator_q), .reset(counter_1_carry));  // open: Qn, preset, en
  // Probe on multiplexer_1_out
  assign adr = writing ? multiplexer_1_out : 16'bz;  // Controlled_Buffer controlled_buffer_1
  assign val = writing ? multiplexer_2_out : 16'bz;  // Controlled_Buffer controlled_buffer_2
  // Probe on multiplexer_2_out
  not not_1 (not_1_out, writing);
  D_Flip_Flop #(.trigger("falling")) synchronizer (
    .clk(clock), .D(activator_q), .Q(writing), .reset(counter_1_carry));  // open: Qn, preset, en
  buf buffer_1 (write, writing);

  // Other names for the same wires on the sheet: clk = clock

  // Notes on the sheet:
  //   buffer_1 drives only 1 and floats otherwise
endmodule

module shot_writer (
  input  [15:0] x,
  input  [15:0] y,
  input  run,
  input  clock,
  output [15:0] adr,
  output [15:0] val,
  output write
);

  wire activator_q, counter_1_carry, not_1_out, not_2_out, writing;
  wire [1:0] bit_extender_1_out;
  wire [2:0] counter_1_q;
  wire [15:0] multiplexer_1_out, multiplexer_2_out;

  Counter #(.width(3), .max('h5)) counter_1 (
    .Q(counter_1_q), .carry(counter_1_carry), .clk(not_1_out), .clr(not_2_out));  // open: load, D, count
  not not_1 (not_1_out, clock);
  Bit_Extender #(.in_width(3), .out_width(2)) bit_extender_1 (.in(counter_1_q), .out(bit_extender_1_out));
  Multiplexer #(.select(2), .width(16), .enable("false")) multiplexer_1 (
    .in0({16{1'b0}}), .in1(16'ha0), .in2(16'ha8), .in3(16'haa), .out(multiplexer_1_out),
    .sel(bit_extender_1_out));
  Multiplexer #(.select(2), .width(16), .enable("false")) multiplexer_2 (
    .in0({16{1'b0}}), .in1(16'h1), .in2(x), .in3(y), .out(multiplexer_2_out), .sel(bit_extender_1_out));
  assign adr = writing ? multiplexer_1_out : 16'bz;  // Controlled_Buffer controlled_buffer_1
  // Probe on multiplexer_1_out
  assign val = writing ? multiplexer_2_out : 16'bz;  // Controlled_Buffer controlled_buffer_2
  // Probe on multiplexer_2_out
  not not_2 (not_2_out, writing);
  D_Flip_Flop activator (.clk(run), .D(run), .Q(activator_q), .reset(counter_1_carry));  // open: Qn, preset, en
  buf buffer_1 (write, writing);
  D_Flip_Flop #(.trigger("falling")) synchronizer (
    .clk(clock), .D(activator_q), .Q(writing), .reset(counter_1_carry));  // open: Qn, preset, en

  // Other names for the same wires on the sheet: clk = clock

  // Notes on the sheet:
  //   buffer_1 drives only 1 and floats otherwise
endmodule

module player_writer (
  input  [15:0] x,
  input  [15:0] y,
  input  run,
  input  clock,
  output [15:0] adr,
  output [15:0] val,
  output write
);

  wire activator_q, counter_1_carry, not_1_out, not_2_out, writing;
  wire [1:0] bit_extender_1_out;
  wire [2:0] counter_1_q;
  wire [15:0] multiplexer_1_out, multiplexer_2_out;

  Counter #(.width(3), .max('h3)) counter_1 (
    .Q(counter_1_q), .carry(counter_1_carry), .clk(not_1_out), .clr(not_2_out));  // open: load, D, count
  not not_1 (not_1_out, clock);
  // Probe on x
  // Probe on y
  Bit_Extender #(.in_width(3), .out_width(2)) bit_extender_1 (.in(counter_1_q), .out(bit_extender_1_out));
  Multiplexer #(.select(2), .width(16), .enable("false")) multiplexer_1 (
    .in0({16{1'b0}}), .in1(16'ha8), .in2(16'haa), .out(multiplexer_1_out), .sel(bit_extender_1_out));  // open: in3
  Multiplexer #(.select(2), .width(16), .enable("false")) multiplexer_2 (
    .in0({16{1'b0}}), .in1(x), .in2(y), .out(multiplexer_2_out), .sel(bit_extender_1_out));  // open: in3
  D_Flip_Flop activator (.clk(run), .D(run), .Q(activator_q), .reset(counter_1_carry));  // open: Qn, preset, en
  assign adr = writing ? multiplexer_1_out : 16'bz;  // Controlled_Buffer controlled_buffer_1
  // Probe on multiplexer_1_out
  assign val = writing ? multiplexer_2_out : 16'bz;  // Controlled_Buffer controlled_buffer_2
  // Probe on multiplexer_2_out
  not not_2 (not_2_out, writing);
  D_Flip_Flop #(.trigger("falling")) synchronizer (
    .clk(clock), .D(activator_q), .Q(writing), .reset(counter_1_carry));  // open: Qn, preset, en
  buf buffer_1 (write, writing);

  // Other names for the same wires on the sheet: clk = clock

  // Notes on the sheet:
  //   buffer_1 drives only 1 and floats otherwise
endmodule

module collision_writer (
  input  [15:0] collided,
  input  run,
  input  clock,
  output [15:0] adr,
  output [15:0] val,
  output write
);

  wire activator_q, counter_1_carry, not_1_out, not_2_out, writing;
  wire [1:0] counter_1_q;
  wire [15:0] multiplexer_1_out, multiplexer_2_out;

  Counter #(.width(2), .max('h2)) counter_1 (
    .Q(counter_1_q), .carry(counter_1_carry), .clk(not_1_out), .clr(not_2_out));  // open: load, D, count
  not not_1 (not_1_out, clock);
  Multiplexer #(.select(2), .width(16), .enable("false")) multiplexer_1 (
    .in0({16{1'b0}}), .in1(16'h94), .out(multiplexer_1_out), .sel(counter_1_q));  // open: in2, in3
  Multiplexer #(.select(2), .width(16), .enable("false")) multiplexer_2 (
    .in0({16{1'b0}}), .in1(collided), .out(multiplexer_2_out), .sel(counter_1_q));  // open: in2, in3
  // Probe on multiplexer_1_out
  assign adr = writing ? multiplexer_1_out : 16'bz;  // Controlled_Buffer controlled_buffer_1
  assign val = writing ? multiplexer_2_out : 16'bz;  // Controlled_Buffer controlled_buffer_2
  // Probe on multiplexer_2_out
  not not_2 (not_2_out, writing);
  D_Flip_Flop activator (.clk(run), .D(run), .Q(activator_q), .reset(counter_1_carry));  // open: Qn, preset, en
  buf buffer_1 (write, writing);
  D_Flip_Flop #(.trigger("falling")) synchronizer (
    .clk(clock), .D(activator_q), .Q(writing), .reset(counter_1_carry));  // open: Qn, preset, en

  // Other names for the same wires on the sheet: clk = clock

  // Notes on the sheet:
  //   buffer_1 drives only 1 and floats otherwise
endmodule

module movement_controller (
  input  left,
  input  right,
  output [2:0] x_vec
);

  wire [2:0] multiplexer_1_out, multiplexer_2_out;

  Multiplexer #(.width(3), .enable("false")) multiplexer_1 (
    .in0(3'b100), .in1(3'b010), .out(multiplexer_1_out), .sel(left));
  Transistor #(.width(3)) transistor_1 (.in(multiplexer_1_out), .out(x_vec), .gate(right));
  Multiplexer #(.width(3), .enable("false")) multiplexer_2 (
    .in0(3'b100), .in1(3'b110), .out(multiplexer_2_out), .sel(right));
  Transistor #(.width(3)) transistor_2 (.in(multiplexer_2_out), .out(x_vec), .gate(left));
endmodule

module hex_to_dec (
  input  [15:0] input_hex,
  output [3:0] output_2,
  output [3:0] output_1
);

  wire [15:0] divider_1_out, divider_1_rem, divider_2_rem;

  Divider #(.width(16)) divider_1 (.a(input_hex), .b(16'ha), .out(divider_1_out), .rem(divider_1_rem));  // open: upper
  Divider #(.width(16)) divider_2 (.a(divider_1_out), .b(16'ha), .rem(divider_2_rem));  // open: out, upper
  Bit_Extender #(.in_width(16), .out_width(4)) bit_extender_1 (.in(divider_2_rem), .out(output_2));
  Bit_Extender #(.in_width(16), .out_width(4)) bit_extender_2 (.in(divider_1_rem), .out(output_1));
endmodule
